# Fritzing sketch Circuit Fritz (saved by Fritzing 0.9.3b)
breadboards: 1

parts:
  Part1 = Arduino Micro (Rev3)  # not connected
  R1 = Photocell (LDR) [package=THT]
  R2 = Resistor [tolerance=±5% resistance=1k package="2512 [SMD]"]
  U1 = XBEE-1 [package=xbee-silk]

nets:
  N1: R1.pin_1, R2.Pin_0
  N2: R2.Pin_1, U1.GND

notes:
  1k Ohm Resistor
  3V -> XBee
  5V -> Photoresistor
  TX -> DIN
  3.3V -> UCC
